// Logisim project part3.circ as structural Verilog: 1 circuit, main circuit main
module main (
  input  a,
  input  b,
  output a_2,
  output a__a_b
);

  wire or_1_out;

  or or_1 (or_1_out, a, b);
  and and_1 (a__a_b, a, or_1_out);

  assign a_2 = a;
endmodule
