// Logisim project part4.circ as structural Verilog: 1 circuit, main circuit main
module main (
  input  C,
  input  D,
  output CD_prime___C_prime_D
);

  wire and_1_out, and_2_out, not_1_out, not_2_out;

  and and_1 (and_1_out, C, not_1_out);
  not not_1 (not_1_out, D);
  not not_2 (not_2_out, C);
  and and_2 (and_2_out, not_2_out, D);
  or or_1 (CD_prime___C_prime_D, and_1_out, and_2_out);
endmodule
