// Logisim project experiment3_logisim.circ as structural Verilog
module full_adder (
  input  C_IN,
  input  A,
  input  B,
  output SUM,
  output sum_2,
  output C_OUT,
  output c
);

  wire and_2_out;

  xor xor_1 (sum_2, A, B);
  and and_1 (c, A, B);
  xor xor_2 (SUM, C_IN, sum_2);
  and and_2 (and_2_out, C_IN, sum_2);
  or or_1 (C_OUT, and_2_out, c);
endmodule

module half_adder (
  input  A,
  input  B,
  output sum,
  output c
);

  xor xor_1 (sum, A, B);
  and and_1 (c, A, B);
endmodule
