// Logisim project MinCostExpressionMUX.circ as structural Verilog: 1 circuit, main circuit main
module main (
  input  D,
  input  A,
  input  B,
  input  C,
  output out_5
);

  wire not_1_out;

  not not_1 (not_1_out, D);
  Multiplexer #(.select(3)) multiplexer_1 (
    .in0(not_1_out), .in1(not_1_out), .in2(1'b0), .in3(1'b1), .in4(not_1_out), .in5(1'b1), .in6(1'b0),
    .in7(D), .out(out_5), .sel({A, B, C}));  // open: en
endmodule
