// Logisim project Preliminary2.circ as structural Verilog: 1 circuit, main circuit main
module main (
  input  A,
  input  B,
  input  C,
  input  A_2,
  input  B_2,
  input  C_2,
  output out_7,
  output out_8
);

  wire decoder_1_out3, decoder_1_out5, decoder_2_out6, decoder_2_out7;

  Decoder #(.select(3), .disabled(0), .enable("false")) decoder_1 (
    .out3(decoder_1_out3), .out5(decoder_1_out5), .sel({A, B, C}));  // open: out0, out1, out2, out4, out6, out7
  Decoder #(.select(3), .disabled(0), .enable("false")) decoder_2 (
    .out6(decoder_2_out6), .out7(decoder_2_out7), .sel({A_2, B_2, C_2}));  // open: out0, out1, out2, out3, out4, out5
  or or_1 (out_7, decoder_1_out3, decoder_1_out5);
  or or_2 (out_8, decoder_2_out6, decoder_2_out7);
endmodule
