// Logisim project part7.circ as structural Verilog: 2 circuits, main circuit main
module main (
  input  [3:0] Input,
  input  Load,
  output Output
);

  wire CLK_out, d_ff_2_q, d_ff_3_q, d_ff_4_q, mux_2_out, mux_3_out, mux_4_out, mux_out, not_1_out, not_2_out,
       not_3_out, not_4_out;

  Clock CLK (.out(CLK_out));
  mux mux (.i0(d_ff_4_q), .i1(Input[3]), .out(mux_out), .s(Load));
  not not_1 (not_1_out, CLK_out);
  D_Flip_Flop #(.trigger("falling")) d_ff_1 (.clk(not_1_out), .D(mux_out), .Q(Output));  // open: Qn, preset, en, reset
  mux mux_2 (.i0(Output), .i1(Input[2]), .out(mux_2_out), .s(Load));
  not not_2 (not_2_out, CLK_out);
  D_Flip_Flop #(.trigger("falling")) d_ff_2 (
    .clk(not_2_out), .D(mux_2_out), .Q(d_ff_2_q));  // open: Qn, preset, en, reset
  not not_3 (not_3_out, CLK_out);
  mux mux_3 (.i0(d_ff_2_q), .i1(Input[1]), .out(mux_3_out), .s(Load));
  D_Flip_Flop #(.trigger("falling")) d_ff_3 (
    .clk(not_3_out), .D(mux_3_out), .Q(d_ff_3_q));  // open: Qn, preset, en, reset
  mux mux_4 (.i0(d_ff_3_q), .i1(Input[0]), .out(mux_4_out), .s(Load));
  not not_4 (not_4_out, CLK_out);
  D_Flip_Flop #(.trigger("falling")) d_ff_4 (
    .clk(not_4_out), .D(mux_4_out), .Q(d_ff_4_q));  // open: Qn, preset, en, reset

  // Notes on the sheet:
  //   feedback wire
endmodule

module mux (
  input  s,
  input  i0,
  input  i1,
  output out
);

  wire and_1_out, and_2_out, not_1_out;

  not not_1 (not_1_out, s);
  and and_1 (and_1_out, not_1_out, i0);
  and and_2 (and_2_out, s, i1);
  or or_1 (out, and_1_out, and_2_out);
endmodule
