// Logisim project MinCostExpression.circ as structural Verilog: 1 circuit, main circuit main
module main (
  input  A,
  input  B,
  input  C,
  input  D,
  input  A_2,
  input  B_2,
  input  C_2,
  input  D_2,
  output out_9,
  output out_10
);

  wire and_1_out, and_2_out, and_3_out, nand_1_out, nand_2_out, nand_3_out, nand_4_out, nand_5_out,
       nand_6_out, not_1_out, not_2_out, not_3_out;

  not not_1 (not_1_out, A);
  not not_2 (not_2_out, B);
  not not_3 (not_3_out, D);
  nand nand_1 (nand_1_out, A_2, A_2);
  nand nand_2 (nand_2_out, B_2, B_2);
  nand nand_3 (nand_3_out, D_2, D_2);
  and and_1 (and_1_out, not_1_out, B, C);
  and and_2 (and_2_out, A, C, D);
  or or_1 (out_9, and_1_out, and_2_out, and_3_out);
  and and_3 (and_3_out, not_2_out, not_3_out);
  nand nand_4 (nand_4_out, nand_1_out, B_2, C_2);
  nand nand_5 (nand_5_out, A_2, C_2, D_2);
  nand nand_6 (nand_6_out, nand_2_out, nand_3_out);
  nand nand_7 (out_10, nand_4_out, nand_5_out, nand_6_out);

  // Notes on the sheet:
  //   Preliminary 1.d.
  //   Preliminary 1.e.
endmodule
