// Logisim project MinCostExpressionNAND.circ as structural Verilog: 1 circuit, main circuit main
module main (
  input  A,
  input  B,
  input  C,
  input  D,
  output x
);

  wire nand_1_out, nand_2_out, nand_3_out, nand_4_out, nand_5_out, nand_6_out;

  nand nand_1 (nand_1_out, A, A);
  nand nand_2 (nand_2_out, B, B);
  nand nand_3 (nand_3_out, D, D);
  nand nand_4 (nand_4_out, nand_1_out, B, C);
  nand nand_5 (nand_5_out, A, C, D);
  nand nand_6 (nand_6_out, nand_2_out, nand_3_out);
  nand nand_7 (x, nand_4_out, nand_5_out, nand_6_out);
endmodule
